# Fritzing sketch led-button-piezo (saved by Fritzing 0.9.3b)
breadboards: 1

parts:
  Part1 = Arduino Uno (Rev3)
  S2 = Momentary Switch [package=ksa_sealed_tac_switch]
  LED2 = smd LED [color="Red (633nm)" package="0603 [SMD]"]
  R2 = Resistor [tolerance=±5% resistance=220 package="0402 [SMD]"]
  J1 = Piezo Speaker

nets:
  N1: Part1.D11_PWM/MOSI, J1.pin1
  N2: Part1.D12/MISO, R2.Pin_1
  N3: Part1.D13/SCK, S2.2
  N4: Part1.D4, J1.pin2
  N5: Part1.GND, S2.4, LED2.cathode
  N6: LED2.anode, R2.Pin_0
