# Fritzing sketch led (saved by Fritzing 0.9.3b)
breadboards: 1

parts:
  Part1 = Arduino Uno (Rev3)
  LED2 = smd LED [color="Red (633nm)" package="0603 [SMD]"]
  R2 = Resistor [tolerance=±5% resistance=220 package="0402 [SMD]"]

nets:
  N1: Part1.D12/MISO, R2.Pin_1
  N2: Part1.GND, LED2.cathode
  N3: LED2.anode, R2.Pin_0
