# Fritzing sketch memory-game (saved by Fritzing 0.9.3b)
breadboards: 1

parts:
  LED2 = smd LED [color="Red (633nm)" package="0603 [SMD]"]
  Part1 = Arduino Uno (Rev3)
  R2 = Resistor [tolerance=±5% resistance=220 package="0402 [SMD]"]
  S2 = Momentary Switch [package=ksa_sealed_tac_switch]
  J1 = Piezo Speaker
  R3 = Resistor [tolerance=±5% resistance=220 package="2010 [SMD]"]
  R1 = Resistor [tolerance=±5% resistance=220 package="0402 [SMD]"]
  S1 = Momentary Switch [package=ksa_sealed_tac_switch]
  LED1 = smd LED [color="Red (633nm)" package="0603 [SMD]"]

nets:
  N1: LED2.cathode, Part1.GND, S2.4, S1.2, LED1.cathode
  N2: LED2.anode, R2.Pin_0
  N3: Part1.D11_PWM/MOSI, J1.pin1
  N4: Part1.D12/MISO, R2.Pin_1
  N5: Part1.D13/SCK, S2.2
  N6: Part1.D2, R3.Pin_1, S1.4
  N7: Part1.D3_PWM, R1.Pin_1
  N8: Part1.D4, J1.pin2
  N9: Part1.5V, R3.Pin_0
  N10: R1.Pin_0, LED1.anode
